// Digital circuit Digital-document.dig as structural Verilog
module Digital_document (
);

  wire _0, _1, _2, _3, _4, _5, _6, _7, _8, _9, add, c, div, eq, err, mult, or_2_out, or_3_out, regadd,
       regdiv, regmult, regsub, sign, start, sub;
  wire [6:0] d0, d1, d2, d3, d4, d5, d6, d7, d8, d9, d10, d11;

  Button u_eq (.out(eq));
  Button u__1 (.out(_1));
  Button u__4 (.out(_4));
  Button u__7 (.out(_7));
  or or_1 (start, or_3_out, or_2_out);
  Button u_c (.out(c));
  Button u__2 (.out(_2));
  Button u__5 (.out(_5));
  Button u__8 (.out(_8));
  Button u__0 (.out(_0));
  Seven_Seg seven_seg_1 (.a(d3[6]), .b(d3[5]), .c(d3[4]), .d(d3[3]), .e(d3[2]), .f(d3[1]), .g(d3[0]), .dp(1'b0));
  or or_2 (or_2_out, _5, _6, _7, _8, _9);
  or or_3 (or_3_out, _0, _1, _2, _3, _4);
  Button u__3 (.out(_3));
  Button u__6 (.out(_6));
  Button u__9 (.out(_9));
  Button plus (.out(add));
  Button button (.out(sub));
  Button button_2 (.out(mult));
  Button button_3 (.out(div));
  Seven_Seg seven_seg_2 (.a(d2[6]), .b(d2[5]), .c(d2[4]), .d(d2[3]), .e(d2[2]), .f(d2[1]), .g(d2[0]), .dp(1'b0));
  Seven_Seg seven_seg_3 (.a(d1[6]), .b(d1[5]), .c(d1[4]), .d(d1[3]), .e(d1[2]), .f(d1[1]), .g(d1[0]), .dp(1'b0));
  Seven_Seg seven_seg_4 (.a(d0[6]), .b(d0[5]), .c(d0[4]), .d(d0[3]), .e(d0[2]), .f(d0[1]), .g(d0[0]), .dp(1'b0));
  LED u_add (.in(regadd));
  LED u_sub (.in(regsub));
  LED u_mult (.in(regmult));
  LED u_div (.in(regdiv));
  Seven_Seg seven_seg_5 (.a(d7[6]), .b(d7[5]), .c(d7[4]), .d(d7[3]), .e(d7[2]), .f(d7[1]), .g(d7[0]), .dp(1'b0));
  calculator #(.applicationType("IVERILOG")) u_calculator (
    .number({_9, _8, _7, _6, _5, _4, _3, _2, _1, _0}), .reset(c), .enter(eq), .start(start), .add(add),
    .sub(sub), .mult(mult), .div(div), .err(err), .sign(sign), .regadd(regadd), .regsub(regsub),
    .regmult(regmult), .regdiv(regdiv), .display0(d0), .display1(d1), .display2(d2), .display3(d3),
    .display4(d4), .display5(d5), .display6(d6), .display7(d7), .display8(d8), .display9(d9),
    .display10(d10), .display11(d11));
  Seven_Seg seven_seg_6 (.a(d6[6]), .b(d6[5]), .c(d6[4]), .d(d6[3]), .e(d6[2]), .f(d6[1]), .g(d6[0]), .dp(1'b0));
  Seven_Seg seven_seg_7 (.a(d5[6]), .b(d5[5]), .c(d5[4]), .d(d5[3]), .e(d5[2]), .f(d5[1]), .g(d5[0]), .dp(1'b0));
  Seven_Seg seven_seg_8 (.a(d4[6]), .b(d4[5]), .c(d4[4]), .d(d4[3]), .e(d4[2]), .f(d4[1]), .g(d4[0]), .dp(1'b0));
  Seven_Seg seven_seg_9 (.a(d11[6]), .b(d11[5]), .c(d11[4]), .d(d11[3]), .e(d11[2]), .f(d11[1]), .g(d11[0]), .dp(1'b0));
  Seven_Seg seven_seg_10 (
    .a(d10[6]), .b(d10[5]), .c(d10[4]), .d(d10[3]), .e(d10[2]), .f(d10[1]), .g(d10[0]), .dp(1'b0));
  Seven_Seg seven_seg_11 (.a(d9[6]), .b(d9[5]), .c(d9[4]), .d(d9[3]), .e(d9[2]), .f(d9[1]), .g(d9[0]), .dp(1'b0));
  Seven_Seg seven_seg_12 (.a(d8[6]), .b(d8[5]), .c(d8[4]), .d(d8[3]), .e(d8[2]), .f(d8[1]), .g(d8[0]), .dp(1'b0));
  LED minus_sign (.in(sign));
  LED error_lamp (.in(err));

  // Other names for the same wires on the sheet: n[9:0] = {_9, _8, _7, _6, _5, _4, _3, _2, _1, _0}
endmodule

/* Code of calculator:
module calculator(
  input wire [9:0] number,
  input wire reset,
  input wire enter,
  input wire start,
  input wire add,
  input wire sub,
  input wire mult,
  input wire div,
  output reg err,
  output reg sign,
  output reg regadd,
  output reg regsub,
  output reg regmult,
  output reg regdiv,
  output reg [6:0] display0,
  output reg [6:0] display1,
  output reg [6:0] display2,
  output reg [6:0] display3,
  output reg [6:0] display4,
  output reg [6:0] display5,
  output reg [6:0] display6,
  output reg [6:0] display7,
  output reg [6:0] display8,
  output reg [6:0] display9,
  output reg [6:0] display10,
  output reg [6:0] display11
);
  reg [3:0] d0, d1, d2, d3, d4, d5, d6, d7, d8, d9, d10, d11;
  reg [15:0] n1, n2, n3;
always @(posedge reset)begin
      display0 <= 7'b1111110;
      display1 <= 7'b1111110;
      display2 <= 7'b1111110;
      display3 <= 7'b1111110;
      display4 <= 7'b1111110;
      display5 <= 7'b1111110;
      display6 <= 7'b1111110;
      display7 <= 7'b1111110;
      display8 <= 7'b1111110;
      display9 <= 7'b1111110;
      display10 <= 7'b1111110;
      display11 <= 7'b1111110;
      regadd <= 0;
      regsub <= 0;
      regmult <= 0;
      regdiv <= 0;
      d0 <= 4'b0;
      d1 <= 4'b0;
      d2 <= 4'b0;
      d3 <= 4'b0;
      d4 <= 4'b0;
      d5 <= 4'b0;
      d6 <= 4'b0;
      d7 <= 4'b0;
      d8 <= 4'b0;
      d9 <= 4'b0;
      d10 <= 4'b0;
      d11 <= 4'b0;
      n1 <= 16'b0;
      n2 <= 16'b0;
      n3 <= 16'b0;
      err <= 0;
      sign <= 0;
end
always @(posedge add or posedge sub or posedge mult or posedge div)begin
	if (add) begin
	regadd <=1;
	end
	else if (sub) begin
	regsub <=1;
	end
	else if (mult) begin
	regmult <=1;
	end
	else if (div) begin
	regdiv <=1;
	end
end
always @(posedge start) begin
     if (regadd == 1 || regsub == 1 || regmult == 1 || regdiv == 1) begin
      display5 <= display4;
      display6 <= display5;
      display7 <= display6;
      d5 <= d4;
      d6 <= d5;
      d7 <= d6;
      case (number)
        10'b0000000001: begin display4 <= 7'b1111110; d4 <= 4'b0000; end
        10'b0000000010: begin display4 <= 7'b0110000; d4 <= 4'b0001; end
        10'b0000000100: begin display4 <= 7'b1101101; d4 <= 4'b0010; end
        10'b0000001000: begin display4 <= 7'b1111001; d4 <= 4'b0011; end
        10'b0000010000: begin display4 <= 7'b0110011; d4 <= 4'b0100; end
        10'b0000100000: begin display4 <= 7'b1011011; d4 <= 4'b0101; end
        10'b0001000000: begin display4 <= 7'b1011111; d4 <= 4'b0110; end
        10'b0010000000: begin display4 <= 7'b1110000; d4 <= 4'b0111; end
        10'b0100000000: begin display4 <= 7'b1111111; d4 <= 4'b1000; end
        10'b1000000000: begin display4 <= 7'b1111011; d4 <= 4'b1001; end
      endcase
    end
    else begin
      display1 <= display0;
      display2 <= display1;
      display3 <= display2;
      d1 <= d0;
      d2 <= d1;
      d3 <= d2;
      case (number)
        10'b0000000001: begin display0 <= 7'b1111110; d0 <= 4'b0000; end
        10'b0000000010: begin display0 <= 7'b0110000; d0 <= 4'b0001; end
        10'b0000000100: begin display0 <= 7'b1101101; d0 <= 4'b0010; end
        10'b0000001000: begin display0 <= 7'b1111001; d0 <= 4'b0011; end
        10'b0000010000: begin display0 <= 7'b0110011; d0 <= 4'b0100; end
        10'b0000100000: begin display0 <= 7'b1011011; d0 <= 4'b0101; end
        10'b0001000000: begin display0 <= 7'b1011111; d0 <= 4'b0110; end
        10'b0010000000: begin display0 <= 7'b1110000; d0 <= 4'b0111; end
        10'b0100000000: begin display0 <= 7'b1111111; d0 <= 4'b1000; end
        10'b1000000000: begin display0 <= 7'b1111011; d0 <= 4'b1001; end
      endcase
end
end
always @(posedge enter) begin
n1 = d0 + 10 * d1 + 100 * d2 + 1000 * d3;
n2 = d4 + 10 * d5 + 100 * d6 + 1000 * d7;
if (n1 >= n2 && regsub == 1) begin
     n3 = n1 - n2;
     d8 = n3 % 10;
     d9 = (n3 % 100) / 10;
     d10 = (n3 % 1000) / 100;
     d11 = (n3 % 10000) / 1000;
     sign = 0;
     end
if (n2 >= n1 && regsub == 1) begin
     n3 = n2 - n1;
     d8 = n3 % 10;
     d9 = (n3 % 100) / 10;
     d10 = (n3 % 1000) / 100;
     d11 = (n3 % 10000) / 1000;
     sign = 1;
     end
if (regadd == 1) begin
     n3 = n1 + n2;
     if (n3 > 9999)begin
	err <= 1;
	n3 = 16'b0;
	end
     d8 = n3 % 10;
     d9 = (n3 % 100) / 10;
     d10 = (n3 % 1000) / 100;
     d11 = (n3 % 10000) / 1000;
     end
if (regmult == 1) begin
     n3 = n1 * n2;
     if (n3 > 9999)begin
	err <= 1;
	n3 = 16'b0;
	end
     d8 = n3 % 10;
     d9 = (n3 % 100) / 10;
     d10 = (n3 % 1000) / 100;
     d11 = (n3 % 10000) / 1000;
     end
if (regdiv == 1 && n2 != 0) begin
     n3 = n1 / n2;
     d8 = n3 % 10;
     d9 = (n3 % 100) / 10;
     d10 = (n3 % 1000) / 100;
     d11 = (n3 % 10000) / 1000; 
     end
if (regdiv == 1 && n2 == 0)begin
     err <= 1;
     end
if (err == 0) begin
	case (d8)
	4'b0000: begin display8 <= 7'b1111110; end
	4'b0001: begin display8 <= 7'b0110000; end
	4'b0010: begin display8 <= 7'b1101101; end
	4'b0011: begin display8 <= 7'b1111001; end
	4'b0100: begin display8 <= 7'b0110011; end
	4'b0101: begin display8 <= 7'b1011011; end
	4'b0110: begin display8 <= 7'b1011111; end
	4'b0111: begin display8 <= 7'b1110000; end
	4'b1000: begin display8 <= 7'b1111111; end
	4'b1001: begin display8 <= 7'b1111011; end
	endcase
        case(d9)
	4'b0000: begin display9 <= 7'b1111110; end
	4'b0001: begin display9 <= 7'b0110000; end
	4'b0010: begin display9 <= 7'b1101101; end
	4'b0011: begin display9 <= 7'b1111001; end
	4'b0100: begin display9 <= 7'b0110011; end
	4'b0101: begin display9 <= 7'b1011011; end
	4'b0110: begin display9 <= 7'b1011111; end
	4'b0111: begin display9 <= 7'b1110000; end
	4'b1000: begin display9 <= 7'b1111111; end
	4'b1001: begin display9 <= 7'b1111011; end
	endcase
        case(d10)
	4'b0000: begin display10 <= 7'b1111110; end
	4'b0001: begin display10 <= 7'b0110000; end
	4'b0010: begin display10 <= 7'b1101101; end
	4'b0011: begin display10 <= 7'b1111001; end
	4'b0100: begin display10 <= 7'b0110011; end
	4'b0101: begin display10 <= 7'b1011011; end
	4'b0110: begin display10 <= 7'b1011111; end
	4'b0111: begin display10 <= 7'b1110000; end
	4'b1000: begin display10 <= 7'b1111111; end
	4'b1001: begin display10 <= 7'b1111011; end
	endcase
        case(d11)
	4'b0000: begin display11 <= 7'b1111110; end
	4'b0001: begin display11 <= 7'b0110000; end
	4'b0010: begin display11 <= 7'b1101101; end
	4'b0011: begin display11 <= 7'b1111001; end
	4'b0100: begin display11 <= 7'b0110011; end
	4'b0101: begin display11 <= 7'b1011011; end
	4'b0110: begin display11 <= 7'b1011111; end
	4'b0111: begin display11 <= 7'b1110000; end
	4'b1000: begin display11 <= 7'b1111111; end
	4'b1001: begin display11 <= 7'b1111011; end
	endcase
end
end
endmodule
*/
